// Logisim project projectfinal345.circ as structural Verilog: 1 circuit, main circuit main
module main (
  input  A2,
  input  A1,
  input  A0,
  input  B0,
  input  A2_2,
  input  A1_2,
  input  A0_2,
  input  B1,
  input  A2_3,
  input  A1_3,
  input  A0_3,
  input  B2,
  output P1,
  output P0,
  output P4,
  output P3,
  output P2,
  output P5
);

  wire adder_1_cout, adder_1_out, adder_3_cout, adder_4_cout, adder_4_out, adder_5_cout, adder_6_cout,
       and_1_out, and_2_out, and_3_out, and_4_out, and_5_out, and_6_out, and_7_out, and_8_out;

  and and_1 (and_1_out, B2, A2_3);
  and and_2 (and_2_out, B1, A2_2);
  Adder #(.width(1)) adder_1 (.a(adder_4_cout), .b(and_2_out), .out(adder_1_out), .cout(adder_1_cout));  // open: cin
  Adder #(.width(1)) adder_2 (.a(adder_1_cout), .b(and_1_out), .out(P4), .cin(adder_3_cout), .cout(P5));
  and and_3 (and_3_out, B0, A2);
  and and_4 (and_4_out, B2, A1_3);
  Adder #(.width(1)) adder_3 (.a(adder_1_out), .b(and_4_out), .out(P3), .cin(adder_5_cout), .cout(adder_3_cout));
  and and_5 (and_5_out, B0, A1);
  and and_6 (and_6_out, B1, A1_2);
  Adder #(.width(1)) adder_4 (.a(and_6_out), .b(and_3_out), .out(adder_4_out), .cin(adder_6_cout), .cout(adder_4_cout));
  and and_7 (and_7_out, B2, A0_3);
  Adder #(.width(1)) adder_5 (.a(adder_4_out), .b(and_7_out), .out(P2), .cout(adder_5_cout));  // open: cin
  and and_8 (and_8_out, B1, A0_2);
  Adder #(.width(1)) adder_6 (.a(and_5_out), .b(and_8_out), .out(P1), .cout(adder_6_cout));  // open: cin
  buf and_9 (P0, B0);  // AND_Gate
endmodule
